// Logisim project logic_circuitA.circ as structural Verilog: 1 circuit, main circuit main
module main (
  input  RD0,
  input  RD1,
  input  RD2,
  input  RD3,
  output RB0
);

  wire or_1_out;

  or or_1 (or_1_out, RD1, RD2, RD3);
  and and_1 (RB0, RD0, or_1_out);
endmodule
