// Logisim project logic_circuitB.circ as structural Verilog: 1 circuit, main circuit main
module main (
  input  RD2,
  input  RD3,
  output RB1,
  output RB2
);

  wire and_1_out, and_2_out, and_3_out, and_4_out, not_1_out, not_2_out;

  not not_1 (not_1_out, RD2);
  not not_2 (not_2_out, RD3);
  and and_1 (and_1_out, not_1_out, not_2_out);
  and and_2 (and_2_out, not_1_out, RD3);
  and and_3 (and_3_out, RD2, not_2_out);
  and and_4 (and_4_out, RD3, RD2);
  or or_1 (RB1, and_1_out, and_4_out);
  or or_2 (RB2, and_2_out, and_3_out);
endmodule
