// Logisim project logic_circuitC.circ as structural Verilog: 1 circuit, main circuit main
module main (
  input  RD2,
  input  RD3,
  output RB2,
  output RB1
);

  wire nand_1_out, nand_2_out, nand_3_out, nand_4_out;

  nand nand_1 (nand_1_out, RD2, RD2);
  nand nand_2 (nand_2_out, RD2, RD3);
  nand nand_3 (nand_3_out, RD3, RD3);
  nand nand_4 (nand_4_out, nand_1_out, nand_3_out);
  nand nand_5 (RB1, nand_4_out, nand_2_out);
  nand nand_6 (RB2, RB1, RB1);
endmodule
