// Logisim project logic_circuitD.circ as structural Verilog: 1 circuit, main circuit main
module main (
  input  RD1,
  input  RD2,
  output RB0,
  output RB1,
  output RB2,
  output RB3,
  output RB4,
  output RB5,
  output RB6,
  output RB7
);

  not not_1 (RB0, RD1);
  not not_2 (RB1, RD2);
  and and_1 (RB2, RD1, RD2);
  or or_1 (RB3, RD1, RD2);
  nand nand_1 (RB4, RD1, RD2);
  nor nor_1 (RB5, RD1, RD2);
  xor xor_1 (RB6, RD1, RD2);
  xnor xnor_1 (RB7, RD1, RD2);
endmodule
