// Logisim project logic_circuit.circ as structural Verilog: 1 circuit, main circuit main
module main (
  input  RD1,
  input  RD4,
  input  RD2,
  input  RD5,
  input  RD3,
  input  RD6,
  output RB1,
  output RB2,
  output RB3,
  output RB4
);

  wire and_1_out, and_2_out, and_3_out, and_4_out, and_5_out, or_1_out, xor_2_out, xor_3_out;

  xor xor_1 (RB1, RD1, RD4);
  and and_1 (and_1_out, RD1, RD4);
  xor xor_2 (xor_2_out, RD2, RD5);
  and and_2 (and_2_out, RD2, RD5);
  xor xor_3 (xor_3_out, RD3, RD6);
  and and_3 (and_3_out, and_1_out, xor_2_out);
  xor xor_4 (RB2, and_1_out, xor_2_out);
  or or_1 (or_1_out, and_3_out, and_2_out);
  xor xor_5 (RB3, or_1_out, xor_3_out);
  and and_4 (and_4_out, or_1_out, xor_3_out);
  and and_5 (and_5_out, RD3, RD6);
  or or_2 (RB4, and_4_out, and_5_out);
endmodule
